# Fritzing sketch project-06 (saved by Fritzing 0.8.3b)
breadboards: 1

parts:
  Part1 = Arduino Uno (Rev3)
  frequency_regulator = Rotary Potentiometer (Small) [maximum_resistance=10kΩ]
  Volume_regulator = Rotary Potentiometer (Small)
  Speaker = Piezo Speaker
  C1 = Electrolytic Capacitor [capacitance=100µF voltage=20V package="100 mil [THT, electrolytic]"]

nets:
  N1: Part1.A0, frequency_regulator.wiper
  N2: Part1.5V, frequency_regulator.leg1, C1.+
  N3: Part1.GND, frequency_regulator.leg2, Volume_regulator.leg1, Speaker.pin2, C1.-
  N4: Volume_regulator.wiper, Speaker.pin1
